# Fritzing sketch diagrama_servo_R4WiFi (saved by Fritzing 1.0.1)

parts:
  Arduino_UNO_R4_WiFi = Arduino UNO R4 WiFi
  Servomotor_MG996R = Basic Servo

nets:
  N1: Arduino_UNO_R4_WiFi.Pin_8, Servomotor_MG996R.vcc
  N2: Arduino_UNO_R4_WiFi.Pin_9, Servomotor_MG996R.gnd
  N3: Arduino_UNO_R4_WiFi.Pin_43, Servomotor_MG996R.pulse

custom parts:
  Arduino UNO R4 WiFi: The Arduino UNO R4 WiFi merges the RA4M1 microprocessor from Renesas with the ESP32-S3 from Espressif, creating an all-in-one tool for makers with enhanced processing power and a diverse array of new peripherals.
