# Fritzing sketch diagrama_servo (saved by Fritzing 1.0.1)
breadboards: 1

parts:
  Arduino_UNO_R4_WiFi = Arduino Uno (Rev3)
  Servomotor_MG996R = Basic Servo
  Fuente_externa_4_pilas = 4 x AAA Battery Mount

nets:
  N1: Arduino_UNO_R4_WiFi.D9_PWM, Servomotor_MG996R.pulse
  GND: Arduino_UNO_R4_WiFi.GND, Servomotor_MG996R.gnd, Fuente_externa_4_pilas.-
  N2: Servomotor_MG996R.vcc, Fuente_externa_4_pilas.+
